# Fritzing sketch Clock (saved by Fritzing 0.9.2b)
circuit board: 12.85cm x 6.27cm

parts:
  Teensy1 = Teensy 2.0
  U2 = HV5522PG [part_number=HV5522PG package=tqfp44]
  R10 = Trimmer Potentiometer [maximum_resistance=22kΩ part_number=A105820-ND package=THT]
  R11 = Trimmer Potentiometer [maximum_resistance=22kΩ part_number=A105820-ND package=THT]
  J1 = female pin header, 2 pins [form="♀ (female)"]
  R12 = Trimmer Potentiometer [maximum_resistance=22kΩ part_number=A105820-ND package=THT]
  R13 = Trimmer Potentiometer [maximum_resistance=22kΩ part_number=A105820-ND package=THT]
  J2 = female pin header, 2 pins [form="♀ (female)"]
  R14 = Trimmer Potentiometer [maximum_resistance=22kΩ part_number=A105820-ND package=THT]
  R15 = Trimmer Potentiometer [maximum_resistance=22kΩ part_number=A105820-ND package=THT]
  J3 = female pin header, 2 pins [form="♀ (female)"]
  Adapter3 = Nixie Tube Riser [package="DIP (Dual Inline) [THT]"]
  Adapter2 = Nixie Tube Riser [package="DIP (Dual Inline) [THT]"]
  U1 = HV5522PG [part_number=HV5522PG package=tqfp44]
  R6 = Resistor [tolerance=±5% resistance=10k package="1206 [SMD]"]
  R4 = Resistor [tolerance=±5% resistance=10k package="1206 [SMD]"]
  R2 = Resistor [tolerance=±5% resistance=10k package="1206 [SMD]"]
  Q3 = NPN-Transistor [package="SOT-23 [SMD]"]
  Q2 = NPN-Transistor [package="SOT-23 [SMD]"]
  Q1 = NPN-Transistor [package="SOT-23 [SMD]"]
  R5 = Resistor [tolerance=±5% resistance=1k package="1206 [SMD]"]
  R3 = Resistor [tolerance=±5% resistance=1k package="1206 [SMD]"]
  R1 = Resistor [tolerance=±5% resistance=1k package="1206 [SMD]"]
  IC1 = DS3231MZ Real Time Clock
  C1 = Capacitor [package=1210]
  Adapter1 = Nixie Tube Riser [package="DIP (Dual Inline) [THT]"]
  C2 = Capacitor [package=1210]
  BAT1 = Battery Holders [package=battcon_12mm_pth]

nets:
  GND: Teensy1.GND, U2.VSS, U1.VSS, Q3.2, Q2.2, Q1.2, IC1.Pin_5, C1.2, C2.2, BAT1.-
  DATA5: Teensy1.B2, R1.Pin_0
  LE5: Teensy1.B3, R3.Pin_0
  CLK5: Teensy1.B7, R5.Pin_0
  SCL: Teensy1.D0, IC1.Pin_8
  SDA: Teensy1.D1, IC1.Pin_7
  5V: Teensy1.VCC, IC1.Pin_2, C1.1
  N1: U2.HV11, Adapter2.8L
  N2: U2.HV12, Adapter2.9L
  N3: U2.HV13, Adapter3.9L
  N4: U2.HV14, Adapter3.8L
  N5: U2.HV15, Adapter3.7L
  N6: U2.HV16, Adapter3.6L
  N7: U2.HV17, Adapter3.5L
  N8: U2.HV18, Adapter3.4L
  N9: U2.HV19, Adapter3.3L
  N10: U2.HV20, Adapter3.8R
  N11: U2.HV21, Adapter3.7R
  N12: U2.HV22, Adapter3.6R
  N13: U2.HV23, Adapter3.5R
  N14: U2.HV24, Adapter3.4R
  N15: U2.HV25, Adapter3.3R
  N16: U2.HV26, Adapter3.2R
  N17: U2.HV27, Adapter3.1R
  N18: U2.HV28, Adapter3.0R
  N19: U2.HV29, Adapter3.9R
  N20: U2.HV30, Adapter3.2L
  N21: U2.HV31, Adapter3.1L
  N22: U2.HV32, Adapter3.0L
  12V: U2.POL, U2.VDD, U2.BL, U1.POL, U1.VDD, U1.BL, R6.Pin_1, R4.Pin_1, R2.Pin_1
  CLK12: U2.CLK, U1.CLK, R6.Pin_0, Q3.1
  LE12: U2.LE, U1.LE, R4.Pin_0, Q2.1
  N23: U2.DATA_IN, U1.DATA_OUT
  N24: U2.HV1, Adapter2.4R
  N25: U2.HV2, Adapter2.5R
  N26: U2.HV3, Adapter2.6R
  N27: U2.HV4, Adapter2.7R
  N28: U2.HV5, Adapter2.8R
  N29: U2.HV6, Adapter2.3L
  N30: U2.HV7, Adapter2.4L
  N31: U2.HV8, Adapter2.5L
  N32: U2.HV9, Adapter2.6L
  N33: U2.HV10, Adapter2.7L
  N34: R10.wiper, Adapter1.+L
  N35: R10.leg2, R11.leg2, J1.pin2
  N36: R11.wiper, Adapter1.+R
  170V: J1.pin1, J2.pin1, J3.pin1
  N37: R12.wiper, Adapter2.+L
  N38: R12.leg2, R13.leg2, J2.pin2
  N39: R13.wiper, Adapter2.+R
  N40: R14.wiper, Adapter3.+L
  N41: R14.leg2, R15.leg2, J3.pin2
  N42: R15.wiper, Adapter3.+R
  N43: Adapter2.1L, U1.HV24
  N44: Adapter2.2L, U1.HV25
  N45: Adapter2.0L, U1.HV23
  N46: Adapter2.1R, U1.HV30
  N47: Adapter2.2R, U1.HV31
  N48: Adapter2.3R, U1.HV32
  N49: Adapter2.9R, U1.HV26
  N50: Adapter2.0R, U1.HV27
  N51: Adapter2.L.R, U1.HV28
  N52: Adapter2.R.R, U1.HV29
  N53: U1.HV11, Adapter1.8L
  N54: U1.HV12, Adapter1.7L
  N55: U1.HV13, Adapter1.6L
  N56: U1.HV14, Adapter1.5L
  N57: U1.HV15, Adapter1.4L
  N58: U1.HV16, Adapter1.3L
  N59: U1.HV17, Adapter1.8R
  N60: U1.HV18, Adapter1.7R
  N61: U1.HV19, Adapter1.6R
  N62: U1.HV20, Adapter1.5R
  N63: U1.HV21, Adapter1.4R
  N64: U1.HV22, Adapter1.3R
  DATA12: U1.DATA_IN, R2.Pin_0, Q1.1
  N65: U1.HV1, Adapter1.0L
  N66: U1.HV2, Adapter1.1L
  N67: U1.HV3, Adapter1.2L
  N68: U1.HV4, Adapter1.9R
  N69: U1.HV5, Adapter1.0R
  N70: U1.HV6, Adapter1.L.R
  N71: U1.HV7, Adapter1.R.R
  N72: U1.HV8, Adapter1.1R
  N73: U1.HV9, Adapter1.2R
  N74: U1.HV10, Adapter1.9L
  N75: Q3.0, R5.Pin_1
  N76: Q2.0, R3.Pin_1
  N77: Q1.0, R1.Pin_1
  N78: IC1.Pin_6, C2.1, BAT1.+

custom parts:
  HV5522PG: High-Voltage Driver Chip (Open-Drain)
  Nixie Tube Riser: A riser to lift nixie tubes from the underlying board.
  DS3231MZ Real Time Clock: DS3231MZ Real Time Clock. SO-8 surface mount version.
